// Logisim project a.circ as structural Verilog: 2 circuits, main circuit main
// aoeu
module main (
  input  A,
  input  B,
  input  C,
  input  D,
  input  A_2,
  input  B_2,
  input  C_2,
  input  D_2,
  input  E,
  output AB,
  output C_D,
  output AB__prime,
  output C_D_2
);

  and and_1 (AB, A, B);
  or or_1 (C_D, C, D);
  nand nand_1 (AB__prime, A_2, B_2);
  nor nor_1 (C_D_2, C_2, ~D_2, E);  // NOR_Gate
endmodule

module comb (
  input  A,
  input  B,
  input  C,
  output out_4
);

  wire and_1_out, not_1_out;

  or or_1 (out_4, and_1_out, not_1_out);
  and and_1 (and_1_out, B, A);
  not not_1 (not_1_out, C);
endmodule
