// Logisim project memory.circ as structural Verilog: 2 circuits, main circuit register
module register (
  input  Edge_Clock,
  input  Edge_In,
  input  Edge_Load,
  input  Edge_Clear,
  input  Level_Clock,
  input  Level_In,
  input  Level_Load,
  input  Level_Clear,
  output R_Edge_Out,
  output F_Edge_Out,
  output H_Level_Out,
  output L_Level_Out
);

  Register #(.width(1)) register_1 (.D(Edge_In), .en(Edge_Load), .Q(R_Edge_Out), .clk(Edge_Clock), .clr(Edge_Clear));
  Register #(.width(1), .trigger("falling")) register_2 (
    .D(Edge_In), .en(Edge_Load), .Q(F_Edge_Out), .clk(Edge_Clock), .clr(Edge_Clear));
  Register #(.width(1), .trigger("high")) register_3 (
    .D(Level_In), .en(Level_Load), .Q(H_Level_Out), .clk(Level_Clock), .clr(Level_Clear));
  Register #(.width(1), .trigger("low")) register_4 (
    .D(Level_In), .en(Level_Load), .Q(L_Level_Out), .clk(Level_Clock), .clr(Level_Clear));
endmodule

module flip_flops (
  input  DT_FlipFlop_Clock,
  input  DT_FlipFlop_Data,
  input  DT_FlipFlop_Load,
  output D_Q1,
  output D_Q0,
  output T_Q1,
  output T_Q0
);

  D_Flip_Flop d_ff_1 (
    .clk(DT_FlipFlop_Clock), .D(DT_FlipFlop_Data), .Q(D_Q1), .Qn(D_Q0), .en(DT_FlipFlop_Load));  // open: preset, reset
  T_Flip_Flop t_ff_1 (
    .clk(DT_FlipFlop_Clock), .T(DT_FlipFlop_Data), .Q(T_Q1), .Qn(T_Q0), .en(DT_FlipFlop_Load));  // open: preset, reset
endmodule
